# Fritzing sketch nightlight (saved by Fritzing 0.8.5b)
breadboards: 1

parts:
  U1 = MCP1702 Voltage Regulator [package="TO92 [THT]"]
  IC1 = ATtiny85 [package=DIL]
  C1 = Ceramic Capacitor [capacitance=100nF package="100 mil [THT, multilayer]"]
  C2 = Ceramic Capacitor [capacitance=100nF package="100 mil [THT, multilayer]"]
  R1 = Resistor [tolerance=±5% resistance=10k package=THT]
  R2 = Resistor [tolerance=±5% resistance=10k package=THT]
  J1 = male pin header, 1 pin [form="♂ (male)"]
  J2 = male pin header, 1 pin [form="♂ (male)"]
  R3 = Photocell (LDR) [package=THT]  # not connected
  J3 = female pin header, 3 pins [form="♀ (female)"]  # not connected
  R4 = Resistor [tolerance=±5% resistance=220 package=THT]  # not connected
  LED1 = LED - 5mm [color="Red (633nm)" package="5 mm [THT]"]  # not connected
  R5 = Resistor [tolerance=±5% resistance=220 package=THT]  # not connected
  R6 = Resistor [tolerance=±5% resistance=10k package=THT]
  Q1 = NPN-Transistor [package="TO92 [THT]"]
  R7 = Resistor [tolerance=±5% resistance=10k package=THT]
  D1 = Rectifier Diode [part_number=1N4001 package="300 mil [THT]"]
  R8 = Resistor [tolerance=±5% resistance=10k package=THT]

nets:
  GND: U1.GND, IC1.GND, C1.0, C2.0, R2.Pin_1, J2.pin1
  N1: U1.Vin, C2.1, R1.Pin_0, J1.pin1
  VCC: U1.Vout, IC1.VCC, C1.1, R6.Pin_0, R8.Pin_0
  N2: IC1.PB5/RESET, R6.Pin_1
  VBAT: R1.Pin_1, R2.Pin_0
  DATA: Q1.E, D1.anode
  N3: Q1.B, R7.Pin_1
  RX: Q1.C
  TX: R7.Pin_0, D1.cathode, R8.Pin_1

custom parts:
  MCP1702 Voltage Regulator: A MCP1702 Low Dropout Fixed Voltage Regulator (available in 1.2V, 1.5V, 1.8V, 2.5V, 2.8V, 3.0V, 3.3V, 4.0V, 5.0V)
